# Fritzing sketch treadmill (saved by Fritzing 0.9.3b)
breadboards: 1

parts:
  JP1 = Header 8 [package=bm08b-srss-tb]
  R5 = Resistor [tolerance=±5% resistance=47k package=THT]
  C1 = Ceramic Capacitor [capacitance=20nF package="100 mil [THT, multilayer]"]
  C2 = Ceramic Capacitor [capacitance=100nF package="100 mil [THT, multilayer]"]
  R6 = Resistor [tolerance=±5% resistance=220 package=THT]
  RPi4_model_B = Raspberry Pi 4B
  3_3V_to_5V = Logic Level Converter

nets:
  GND: JP1.1, C1.0, C2.0, RPi4_model_B.GND, 3_3V_to_5V.GND
  N1: JP1.3, R5.Pin_0
  N2: JP1.4, 3_3V_to_5V.TX_HV
  N3: JP1.5, RPi4_model_B.GPIO21
  N4: JP1.6, RPi4_model_B.GPIO20
  N5: JP1.7, R6.Pin_1
  N6: R5.Pin_1, C1.1
  N7: C2.1, R6.Pin_0, RPi4_model_B.GPIO16
  N8: RPi4_model_B.3V3, 3_3V_to_5V.LV
  N9: RPi4_model_B.5V, 3_3V_to_5V.HV
  N10: RPi4_model_B.GPIO18, 3_3V_to_5V.TX_LV

notes:
  1 - Black, ground
  2 - Red, +9 VDC
  3 - Green, Speed sensor, 0-5 VDC
  4 - Blue, PWM signal to set speed
  5 - Orange, Incline up
  6 - Yellow, Incline down
  7 - Violet, Incline sensor
  8 - Striped black, step counter (MC2100SDI)
